# Fritzing sketch TheC64-Joystick-Adapter_schematic (saved by Fritzing 0.9.3b)
perfboards: 1

parts:
  Digispark1 = Digispark
  R1 = Resistor [tolerance=±5% resistance=10k package=THT]
  R2 = Resistor [tolerance=±5% resistance=10k package=THT]
  R3 = Resistor [tolerance=±5% resistance=10k package=THT]
  R4 = Resistor [tolerance=±5% resistance=10k package=THT]
  R5 = Resistor [tolerance=±5% resistance=10k package=THT]
  R6 = Resistor [tolerance=±5% resistance=10k package=THT]
  R7 = Resistor [tolerance=±5% resistance=10k package=THT]
  R8 = Resistor [tolerance=±5% resistance=10k package=THT]
  S1 = Pushbutton [package="[THT]"]
  S2 = Pushbutton [package="[THT]"]
  S3 = Pushbutton [package="[THT]"]
  IC1 = IC, DIP package, 16 pins [chip_label=74C151]
  X1 = DB9 Connector [package=db9]

nets (from the breadboard view):
  N1: Digispark1.VCC, R1.Pin_0, R2.Pin_0, R3.Pin_0, R4.Pin_0, R5.Pin_1, R6.Pin_1, R7.Pin_1, R8.Pin_1, IC1.pin16
  N2: Digispark1.GND, S1.Pin_1, S1.Pin_2, S2.Pin_1, S2.Pin_2, S3.Pin_1, S3.Pin_2, IC1.pin7, IC1.pin8, X1.2
  N3: Digispark1.P0, IC1.pin9
  N4: Digispark1.P1, IC1.pin10
  N5: Digispark1.P2, IC1.pin11
  N6: Digispark1.P5, IC1.pin5
  N7: R2.Pin_1, S1.Pin_3, S1.Pin_4, IC1.pin14
  N8: R3.Pin_1, S2.Pin_3, S2.Pin_4, IC1.pin13
  N9: R4.Pin_1, S3.Pin_3, S3.Pin_4, IC1.pin12
  N10: R5.Pin_0, IC1.pin1, X1.6
  N11: R6.Pin_0, IC1.pin2, X1.7
  N12: R7.Pin_0, IC1.pin3, X1.8
  N13: R8.Pin_0, IC1.pin4, X1.9
  N14: IC1.pin15, X1.4

notes:
  Pinout DB9:
  1:UP
  2:Down
  3:Left
  4:Right
  5:+5V (N/A)
  6:Button 1
  7:Button 2 (N/A)
  8:Common
  9:GND

custom parts:
  Digispark: The Digispark is an Attiny85 based microcontroller development board similar to the Arduino line, only cheaper, smaller, and a bit less powerful. With a whole host of shields to extend its functionality and the ability to use the familiar Arduino IDE the Digispark is a great way to jump into electronics, or perfect for when an Arduino is too big or too much.
